# Fritzing sketch SubMarine (saved by Fritzing 0.9.6b)

parts:
  MH-ET_Live_Minikit_for_ESP1 = MH-ET Live Minikit for ESP32
  TP1 = TP4056 [chip_label=TP4056 package="DIP (Dual Inline) [THT]"]
  Bat1 = battery_holder_single_18650
  M1 = cc1101 module
  U1 = SWITCH_SPDT [package=kps-1290]

nets:
  N1: MH-ET_Live_Minikit_for_ESP1.TMS, M1.pin_4
  N2: MH-ET_Live_Minikit_for_ESP1.TCK, MH-ET_Live_Minikit_for_ESP1.SD3, M1.pin_3
  N3: MH-ET_Live_Minikit_for_ESP1.GND, TP1.pin6, M1.pin_9, M1.pin_10
  N4: MH-ET_Live_Minikit_for_ESP1.VCC, M1.pin_1, M1.pin_2, U1.S
  N5: MH-ET_Live_Minikit_for_ESP1.TDO, MH-ET_Live_Minikit_for_ESP1.SD0, M1.pin_7
  N6: MH-ET_Live_Minikit_for_ESP1.TDI, M1.pin_5
  N7: MH-ET_Live_Minikit_for_ESP1.IO4, M1.pin_6
  N8: MH-ET_Live_Minikit_for_ESP1.IO2, M1.pin_8
  N9: TP1.pin3, U1.O
  N10: TP1.pin4, Bat1.+#1
  N11: TP1.pin5, Bat1.+#0

custom parts:
  MH-ET Live Minikit for ESP32: MH-ET Live Minikit for ESP32 ( http://mh.nodebb.com/topic/8/mh-et-live-minikit-for-esp32/2/) PCB footprint is invalid.
  TP4056: A DIP stand-in part for whatever IC you want. With 6 pins on a 300mil dual inline package (DIP) footprint.
  battery_holder_single_18650: single 18650 battery holder
  cc1101 module: CC1101 rf module.
