# Fritzing sketch SubMarineBasic (saved by Fritzing 0.9.6b)

parts:
  MH-ET_Live_Minikit_for_ESP1 = MH-ET Live Minikit for ESP32
  M1 = cc1101 module

nets:
  N1: MH-ET_Live_Minikit_for_ESP1.TMS, M1.pin_4
  N2: MH-ET_Live_Minikit_for_ESP1.TCK, MH-ET_Live_Minikit_for_ESP1.SD3, M1.pin_3
  N3: MH-ET_Live_Minikit_for_ESP1.GND, M1.pin_9, M1.pin_10
  N4: MH-ET_Live_Minikit_for_ESP1.VCC, M1.pin_1, M1.pin_2
  N5: MH-ET_Live_Minikit_for_ESP1.TDO, MH-ET_Live_Minikit_for_ESP1.SD0, M1.pin_7
  N6: MH-ET_Live_Minikit_for_ESP1.TDI, M1.pin_5
  N7: MH-ET_Live_Minikit_for_ESP1.IO4, M1.pin_6
  N8: MH-ET_Live_Minikit_for_ESP1.IO2, M1.pin_8

custom parts:
  MH-ET Live Minikit for ESP32: MH-ET Live Minikit for ESP32 ( http://mh.nodebb.com/topic/8/mh-et-live-minikit-for-esp32/2/) PCB footprint is invalid.
  cc1101 module: CC1101 rf module.
